// Logisim project control-logic.circ as structural Verilog: 1 circuit, main circuit control_logic
module control_logic (
  input  [31:0] Instruction,
  input  BrEq,
  input  BrLt,
  output PCSel,
  output RegWEn,
  output [2:0] ImmSel,
  output BrUn,
  output ASel,
  output BSel,
  output [3:0] ALUSel,
  output MemRW,
  output [1:0] WBSel
);

  wire and_1_out, and_2_out, and_3_out, and_4_out, is_add, is_addi, is_and, is_andi, is_auipc, is_beq,
       is_bge, is_bgeu, is_blt, is_bltu, is_bne, is_jal, is_jalr, is_lb, is_lh, is_lui, is_lw, is_mul,
       is_mulh, is_mulhu, is_or, is_ori, is_sb, is_sh, is_sll, is_slli, is_slt, is_slti, is_sra, is_srai,
       is_srl, is_srli, is_sub, is_sw, is_xor, is_xori, not_1_out, not_2_out, not_3_out, or_1_out, or_2_out;
  wire [5:0] Control;
  wire [15:14] rom_1_data;

  Comparator #(.width(17)) comparator_1 (
    .a({Instruction[31:25], Instruction[14:12], Instruction[6:0]}), .b(17'h3b3), .eq(is_and));  // open: gt, lt
  Comparator #(.width(17)) comparator_2 (
    .a({Instruction[31:25], Instruction[14:12], Instruction[6:0]}), .b(17'h33), .eq(is_add));  // open: gt, lt
  Comparator #(.width(17)) comparator_3 (
    .a({Instruction[31:25], Instruction[14:12], Instruction[6:0]}), .b(17'h433), .eq(is_mul));  // open: gt, lt
  Comparator #(.width(17)) comparator_4 (
    .a({Instruction[31:25], Instruction[14:12], Instruction[6:0]}), .b(17'h8033), .eq(is_sub));  // open: gt, lt
  Comparator #(.width(17)) comparator_5 (
    .a({Instruction[31:25], Instruction[14:12], Instruction[6:0]}), .b(17'hb3), .eq(is_sll));  // open: gt, lt
  Comparator #(.width(17)) comparator_6 (
    .a({Instruction[31:25], Instruction[14:12], Instruction[6:0]}), .b(17'h4b3), .eq(is_mulh));  // open: gt, lt
  Comparator #(.width(17)) comparator_7 (
    .a({Instruction[31:25], Instruction[14:12], Instruction[6:0]}), .b(17'h5b3), .eq(is_mulhu));  // open: gt, lt
  Comparator #(.width(17)) comparator_8 (
    .a({Instruction[31:25], Instruction[14:12], Instruction[6:0]}), .b(17'h133), .eq(is_slt));  // open: gt, lt
  Comparator #(.width(17)) comparator_9 (
    .a({Instruction[31:25], Instruction[14:12], Instruction[6:0]}), .b(17'h233), .eq(is_xor));  // open: gt, lt
  Comparator #(.width(17)) comparator_10 (
    .a({Instruction[31:25], Instruction[14:12], Instruction[6:0]}), .b(17'h2b3), .eq(is_srl));  // open: gt, lt
  Comparator #(.width(17)) comparator_11 (
    .a({Instruction[31:25], Instruction[14:12], Instruction[6:0]}), .b(17'h82b3), .eq(is_sra));  // open: gt, lt
  Comparator #(.width(17)) comparator_12 (
    .a({Instruction[31:25], Instruction[14:12], Instruction[6:0]}), .b(17'h333), .eq(is_or));  // open: gt, lt
  ROM #(.addrWidth(6), .dataWidth(16)) rom_1 (
    .addr(Control), .data({rom_1_data, WBSel, MemRW, ALUSel, BSel, ASel, BrUn, ImmSel, RegWEn}));
  Comparator #(.width(10)) comparator_13 (
    .a({Instruction[14:12], Instruction[6:0]}), .b(10'h3), .eq(is_lb));  // open: gt, lt
  Comparator #(.width(10)) comparator_14 (
    .a({Instruction[14:12], Instruction[6:0]}), .b(10'h83), .eq(is_lh));  // open: gt, lt
  Comparator #(.width(10)) comparator_15 (
    .a({Instruction[14:12], Instruction[6:0]}), .b(10'h103), .eq(is_lw));  // open: gt, lt
  Comparator #(.width(10)) comparator_16 (
    .a({Instruction[14:12], Instruction[6:0]}), .b(10'h13), .eq(is_addi));  // open: gt, lt
  Comparator #(.width(17)) comparator_17 (
    .a({Instruction[31:25], Instruction[14:12], Instruction[6:0]}), .b(17'h93), .eq(is_slli));  // open: gt, lt
  Comparator #(.width(10)) comparator_18 (
    .a({Instruction[14:12], Instruction[6:0]}), .b(10'h113), .eq(is_slti));  // open: gt, lt
  Comparator #(.width(10)) comparator_19 (
    .a({Instruction[14:12], Instruction[6:0]}), .b(10'h213), .eq(is_xori));  // open: gt, lt
  Comparator #(.width(17)) comparator_20 (
    .a({Instruction[31:25], Instruction[14:12], Instruction[6:0]}), .b(17'h293), .eq(is_srli));  // open: gt, lt
  Comparator #(.width(17)) comparator_21 (
    .a({Instruction[31:25], Instruction[14:12], Instruction[6:0]}), .b(17'h8293), .eq(is_srai));  // open: gt, lt
  Comparator #(.width(10)) comparator_22 (
    .a({Instruction[14:12], Instruction[6:0]}), .b(10'h313), .eq(is_ori));  // open: gt, lt
  Comparator #(.width(10)) comparator_23 (
    .a({Instruction[14:12], Instruction[6:0]}), .b(10'h393), .eq(is_andi));  // open: gt, lt
  Priority_Encoder #(.select_enc(6)) priority_encoder_1 (
    .in0(is_add), .in1(is_mul), .in2(is_sub), .in3(is_sll), .in4(is_mulh), .in5(is_mulhu), .in6(is_slt),
    .in7(is_xor), .in8(is_srl), .in9(is_sra), .in10(is_or), .in11(is_and), .in12(is_lb), .in13(is_lh),
    .in14(is_lw), .in15(is_addi), .in16(is_slli), .in17(is_slti), .in18(is_xori), .in19(is_srli),
    .in20(is_srai), .in21(is_ori), .in22(is_andi), .in23(is_sb), .in24(is_sh), .in25(is_sw), .in26(is_beq),
    .in27(is_bne), .in28(is_blt), .in29(is_bge), .in30(is_bltu), .in31(is_bgeu), .in32(is_auipc),
    .in33(is_lui), .in34(is_jal), .in35(is_jalr), .out(Control));  // open: in36, in37, in38, in39, in40, in41, in42, in43, in44, in45, in46, in47, in48, in49, in50, in51, in52, in53, in54, in55, in56, in57, in58, in59, in60, in61, in62, in63, gs, en_out, en_in
  // Probe on Control
  not not_1 (not_1_out, BrEq);
  not not_2 (not_2_out, BrLt);
  Comparator #(.width(10)) comparator_24 (
    .a({Instruction[14:12], Instruction[6:0]}), .b(10'h23), .eq(is_sb));  // open: gt, lt
  Comparator #(.width(10)) comparator_25 (
    .a({Instruction[14:12], Instruction[6:0]}), .b(10'ha3), .eq(is_sh));  // open: gt, lt
  Comparator #(.width(17)) comparator_26 (
    .a({Instruction[31:25], Instruction[14:12], Instruction[6:0]}), .b(17'h123), .eq(is_sw));  // open: gt, lt
  Comparator #(.width(10)) comparator_27 (
    .a({Instruction[14:12], Instruction[6:0]}), .b(10'h63), .eq(is_beq));  // open: gt, lt
  Comparator #(.width(10)) comparator_28 (
    .a({Instruction[14:12], Instruction[6:0]}), .b(10'he3), .eq(is_bne));  // open: gt, lt
  Comparator #(.width(17)) comparator_29 (
    .a({Instruction[31:25], Instruction[14:12], Instruction[6:0]}), .b(17'h263), .eq(is_blt));  // open: gt, lt
  Comparator #(.width(17)) comparator_30 (
    .a({Instruction[31:25], Instruction[14:12], Instruction[6:0]}), .b(17'h2e3), .eq(is_bge));  // open: gt, lt
  Comparator #(.width(10)) comparator_31 (
    .a({Instruction[14:12], Instruction[6:0]}), .b(10'h363), .eq(is_bltu));  // open: gt, lt
  not not_3 (not_3_out, BrEq);
  or or_1 (or_1_out, is_blt, is_bltu);
  or or_2 (or_2_out, is_bge, is_bgeu);
  Comparator #(.width(10)) comparator_32 (
    .a({Instruction[14:12], Instruction[6:0]}), .b(10'h3e3), .eq(is_bgeu));  // open: gt, lt
  and and_1 (and_1_out, is_beq, BrEq);
  and and_2 (and_2_out, is_bne, not_3_out);
  and and_3 (and_3_out, or_1_out, BrLt);
  and and_4 (and_4_out, or_2_out, not_1_out, not_2_out);
  or or_3 (PCSel, and_1_out, and_2_out, and_3_out, and_4_out);
  Comparator #(.width(7)) comparator_33 (.a(Instruction[6:0]), .b(7'b0010111), .eq(is_auipc));  // open: gt, lt
  Comparator #(.width(7)) comparator_34 (.a(Instruction[6:0]), .b(7'b0110111), .eq(is_lui));  // open: gt, lt
  Comparator #(.width(7)) comparator_35 (.a(Instruction[6:0]), .b(7'b1101111), .eq(is_jal));  // open: gt, lt
  Comparator #(.width(10)) comparator_36 (
    .a({Instruction[14:12], Instruction[6:0]}), .b(10'h67), .eq(is_jalr));  // open: gt, lt

  // Other names for the same wires on the sheet: Funct7[6:0] = Instruction[31:25]; Opcode[6:0] = Instruction[6:0];
  //   Funct3[2:0] = Instruction[14:12]

  // Notes on the sheet:
  //   INPUTS to your circuit
  //   contents of rom_1 (hex, n*v repeats v):
  //   1001 1401 1601 1081 1481 1581 1101 1201 1281 1681 1301 1381 41 41 41 1041 10c1 1141 1241 12c1 16c1
  //   1341 13c1 842 842 842 4*64 74 74 1067 17c7 2069 2041
  //   ROM FOR CONTROL LOGIC
  //   DON'T CHANGE THE LOCATIONS OF THE INPUTS AND OUTPUTS!
  //   This is only if you choose to do the ROM option
  //   OUTPUT from your circuit
endmodule
